# Fritzing sketch breadboard_schematic (saved by Fritzing 0.9.3b)
breadboards: 1

parts:
  Part1 = Arduino Nano (Rev3.0)
  SX1 = LAMBDA80C-24D [chip_label=SX1280 package="DIP (Dual Inline) [THT]"]

nets:
  N1: Part1.GND, SX1.pin2
  N2: Part1.D3, SX1.pin7
  N3: Part1.D7, SX1.pin6
  N4: Part1.D9, SX1.pin12
  N5: Part1.D10, SX1.pin16
  N6: Part1.D11/MOSI, SX1.pin15
  N7: Part1.D12/MISO, SX1.pin14
  N8: Part1.D13/SCK, SX1.pin13

custom parts:
  LAMBDA80C-24D: SX1280 Module
